# Fritzing sketch LCD CON SENSORE TEMPERATURA (saved by Fritzing 0.9.3b)
breadboards: 1

parts:
  DHT1 = Humidity and Temperature Sensor DHT11
  Componente1 = Arduino Uno (Rev3)
  RE1 = Rotary Encoder [package=THT]
  LCD1 = LCD screen

nets:
  VCC: DHT1.Vcc, Componente1.5V, RE1.EncoderPinA, LCD1.VDD
  N1: DHT1.Data-signal, Componente1.D8
  GND: DHT1.GND_2, Componente1.GND, RE1.EncoderPinB, LCD1.VSS, LCD1.R/W
  N2: Componente1.D11_PWM/MOSI, LCD1.E
  N3: Componente1.D12/MISO, LCD1.RS
  N4: Componente1.D2, LCD1.DB7
  N5: Componente1.D3_PWM, LCD1.DB6
  N6: Componente1.D4, LCD1.DB5
  N7: Componente1.D5_PWM, LCD1.DB4

custom parts:
  Humidity and Temperature Sensor DHT11: Digital relative humidity & temperature sensor DHT11
