# Fritzing sketch LCD MULTIPIN (saved by Fritzing 0.9.3b)

parts:
  Componente1 = Arduino Uno (Rev3)
  RE1 = Rotary Encoder [package=THT]
  LCD1 = LCD screen

nets:
  N1: Componente1.D11_PWM/MOSI, LCD1.E
  N2: Componente1.D12/MISO, LCD1.RS
  GND: Componente1.GND, RE1.EncoderPinA, LCD1.VSS, LCD1.R/W
  N3: Componente1.D2, LCD1.DB7
  N4: Componente1.D3_PWM, LCD1.DB6
  N5: Componente1.D4, LCD1.DB5
  N6: Componente1.D5_PWM, LCD1.DB4
  5V: Componente1.5V, LCD1.VDD
  N7: RE1.EncoderPinC, LCD1.V0
